// Logisim project 150120006_150121921_524123004_150120942.circ as structural Verilog
module testing (
  input  [9:0] in_1,
  input  [17:0] in_2,
  input  in_3,
  input  in_4,
  input  in_5,
  input  in_6,
  input  in_7,
  input  in_8,
  output [17:0] out_9,
  output out_10
);

  or or_1 (out_10, out_10, in_8);
  RAM #(.addrWidth(10), .dataWidth(18), .bus("separate")) ram_1 (
    .addr(in_1), .din(in_2), .data(out_9), .str(in_3), .sel(in_5), .clk(in_7), .ld(in_6), .clr(in_4));

  // Notes on the sheet:
  //   out_10: pull=down
endmodule

module D_Flip_Flop (
  input  D,
  input  Clk,
  output Q
);

  wire and_1_out, and_2_out, and_3_out, and_4_out, nor_1_out, nor_2_out, nor_3_out, not_1_out, not_2_out,
       not_3_out;

  not not_1 (not_1_out, D);
  not not_2 (not_2_out, Clk);
  and and_1 (and_1_out, D, not_2_out);
  and and_2 (and_2_out, not_2_out, not_1_out);
  nor nor_1 (nor_1_out, and_1_out, nor_2_out);
  nor nor_2 (nor_2_out, nor_1_out, and_2_out);
  not not_3 (not_3_out, nor_2_out);
  and and_3 (and_3_out, nor_2_out, Clk);
  and and_4 (and_4_out, Clk, not_3_out);
  nor nor_3 (nor_3_out, and_3_out, Q);
  nor nor_4 (Q, nor_3_out, and_4_out);
endmodule

module Register (
  input  [17:0] I,
  input  initialise,
  input  load,
  input  clk,
  output [17:0] Q
);

  wire or_1_out;
  wire [17:0] multiplexer_1_out, multiplexer_2_out;

  Multiplexer #(.width(18), .enable("false")) multiplexer_1 (
    .in0(I), .in1({18{1'b0}}), .out(multiplexer_1_out), .sel(initialise));
  or or_1 (or_1_out, initialise, load);
  Multiplexer #(.width(18), .enable("false")) multiplexer_2 (
    .in0(multiplexer_2_out), .in1(multiplexer_1_out), .out(multiplexer_2_out), .sel(or_1_out));
  D_Flip_Flop d_flip_flop_1 (.D(multiplexer_2_out[16]), .Q(Q[16]), .Clk(clk));
  D_Flip_Flop d_flip_flop_2 (.D(multiplexer_2_out[17]), .Q(Q[17]), .Clk(clk));
  D_Flip_Flop d_flip_flop_3 (.D(multiplexer_2_out[15]), .Q(Q[15]), .Clk(clk));
  D_Flip_Flop d_flip_flop_4 (.D(multiplexer_2_out[14]), .Q(Q[14]), .Clk(clk));
  D_Flip_Flop d_flip_flop_5 (.D(multiplexer_2_out[13]), .Q(Q[13]), .Clk(clk));
  D_Flip_Flop d_flip_flop_6 (.D(multiplexer_2_out[12]), .Q(Q[12]), .Clk(clk));
  D_Flip_Flop d_flip_flop_7 (.D(multiplexer_2_out[11]), .Q(Q[11]), .Clk(clk));
  D_Flip_Flop d_flip_flop_8 (.D(multiplexer_2_out[10]), .Q(Q[10]), .Clk(clk));
  D_Flip_Flop d_flip_flop_9 (.D(multiplexer_2_out[8]), .Q(Q[8]), .Clk(clk));
  D_Flip_Flop d_flip_flop_10 (.D(multiplexer_2_out[9]), .Q(Q[9]), .Clk(clk));
  D_Flip_Flop d_flip_flop_11 (.D(multiplexer_2_out[7]), .Q(Q[7]), .Clk(clk));
  D_Flip_Flop d_flip_flop_12 (.D(multiplexer_2_out[6]), .Q(Q[6]), .Clk(clk));
  D_Flip_Flop d_flip_flop_13 (.D(multiplexer_2_out[5]), .Q(Q[5]), .Clk(clk));
  D_Flip_Flop d_flip_flop_14 (.D(multiplexer_2_out[4]), .Q(Q[4]), .Clk(clk));
  D_Flip_Flop d_flip_flop_15 (.D(multiplexer_2_out[3]), .Q(Q[3]), .Clk(clk));
  D_Flip_Flop d_flip_flop_16 (.D(multiplexer_2_out[2]), .Q(Q[2]), .Clk(clk));
  D_Flip_Flop d_flip_flop_17 (.D(multiplexer_2_out[1]), .Q(Q[1]), .Clk(clk));
  D_Flip_Flop d_flip_flop_18 (.D(multiplexer_2_out[0]), .Q(Q[0]), .Clk(clk));
endmodule

module Comparator (
  input  [17:0] number_2,
  input  [17:0] number_1,
  output CARRY_FLAG,
  output ZERO_FLAG
);

  wire or_1_out, or_2_out, or_3_out, or_4_out, or_5_out, or_6_out, subtractor_1_new_carry,
       subtractor_1_result, subtractor_2_new_carry, subtractor_2_result, subtractor_3_new_carry,
       subtractor_3_result, subtractor_4_new_carry, subtractor_4_result, subtractor_5_new_carry,
       subtractor_5_result, subtractor_6_new_carry, subtractor_6_result, subtractor_7_new_carry,
       subtractor_7_result, subtractor_8_new_carry, subtractor_8_result, subtractor_9_new_carry,
       subtractor_9_result, subtractor_10_new_carry, subtractor_10_result, subtractor_11_new_carry,
       subtractor_11_result, subtractor_12_new_carry, subtractor_12_result, subtractor_13_new_carry,
       subtractor_13_result, subtractor_14_new_carry, subtractor_14_result, subtractor_15_new_carry,
       subtractor_15_result, subtractor_16_new_carry, subtractor_16_result, subtractor_17_new_carry,
       subtractor_17_result, subtractor_18_new_carry, subtractor_18_result;

  Subtractor subtractor_1 (
    .number_1(number_1[17]), .number_2(number_2[17]), .carry(subtractor_2_new_carry),
    .result(subtractor_1_result), .new_carry(subtractor_1_new_carry));
  and and_1 (CARRY_FLAG, subtractor_1_new_carry, or_4_out);
  Subtractor subtractor_2 (
    .number_1(number_1[16]), .number_2(number_2[16]), .carry(subtractor_4_new_carry),
    .result(subtractor_2_result), .new_carry(subtractor_2_new_carry));
  or or_1 (or_1_out, subtractor_1_result, subtractor_2_result);
  Subtractor subtractor_3 (
    .number_1(number_1[14]), .number_2(number_2[14]), .carry(subtractor_6_new_carry),
    .result(subtractor_3_result), .new_carry(subtractor_3_new_carry));
  Subtractor subtractor_4 (
    .number_1(number_1[15]), .number_2(number_2[15]), .carry(subtractor_3_new_carry),
    .result(subtractor_4_result), .new_carry(subtractor_4_new_carry));
  Subtractor subtractor_5 (
    .number_1(number_1[12]), .number_2(number_2[12]), .carry(subtractor_7_new_carry),
    .result(subtractor_5_result), .new_carry(subtractor_5_new_carry));
  Subtractor subtractor_6 (
    .number_1(number_1[13]), .number_2(number_2[13]), .carry(subtractor_5_new_carry),
    .result(subtractor_6_result), .new_carry(subtractor_6_new_carry));
  or or_2 (or_2_out, subtractor_4_result, subtractor_3_result, subtractor_6_result, subtractor_5_result);
  Subtractor subtractor_7 (
    .number_1(number_1[11]), .number_2(number_2[11]), .carry(subtractor_8_new_carry),
    .result(subtractor_7_result), .new_carry(subtractor_7_new_carry));
  Subtractor subtractor_8 (
    .number_1(number_1[10]), .number_2(number_2[10]), .carry(subtractor_10_new_carry),
    .result(subtractor_8_result), .new_carry(subtractor_8_new_carry));
  Subtractor subtractor_9 (
    .number_1(number_1[8]), .number_2(number_2[8]), .carry(subtractor_11_new_carry),
    .result(subtractor_9_result), .new_carry(subtractor_9_new_carry));
  Subtractor subtractor_10 (
    .number_1(number_1[9]), .number_2(number_2[9]), .carry(subtractor_9_new_carry),
    .result(subtractor_10_result), .new_carry(subtractor_10_new_carry));
  or or_3 (or_3_out, subtractor_7_result, subtractor_8_result, subtractor_10_result, subtractor_9_result);
  or or_4 (or_4_out, or_1_out, or_2_out, or_3_out, or_5_out, or_6_out);
  not not_1 (ZERO_FLAG, or_4_out);
  Subtractor subtractor_11 (
    .number_1(number_1[7]), .number_2(number_2[7]), .carry(subtractor_13_new_carry),
    .result(subtractor_11_result), .new_carry(subtractor_11_new_carry));
  Subtractor subtractor_12 (
    .number_1(number_1[5]), .number_2(number_2[5]), .carry(subtractor_14_new_carry),
    .result(subtractor_12_result), .new_carry(subtractor_12_new_carry));
  Subtractor subtractor_13 (
    .number_1(number_1[6]), .number_2(number_2[6]), .carry(subtractor_12_new_carry),
    .result(subtractor_13_result), .new_carry(subtractor_13_new_carry));
  or or_5 (or_5_out, subtractor_11_result, subtractor_13_result, subtractor_12_result, subtractor_14_result);
  Subtractor subtractor_14 (
    .number_1(number_1[4]), .number_2(number_2[4]), .carry(subtractor_16_new_carry),
    .result(subtractor_14_result), .new_carry(subtractor_14_new_carry));
  Subtractor subtractor_15 (
    .number_1(number_1[2]), .number_2(number_2[2]), .carry(subtractor_18_new_carry),
    .result(subtractor_15_result), .new_carry(subtractor_15_new_carry));
  Subtractor subtractor_16 (
    .number_1(number_1[3]), .number_2(number_2[3]), .carry(subtractor_15_new_carry),
    .result(subtractor_16_result), .new_carry(subtractor_16_new_carry));
  Subtractor subtractor_17 (
    .number_1(number_1[0]), .number_2(number_2[0]), .carry(1'b0), .result(subtractor_17_result),
    .new_carry(subtractor_17_new_carry));
  Subtractor subtractor_18 (
    .number_1(number_1[1]), .number_2(number_2[1]), .carry(subtractor_17_new_carry),
    .result(subtractor_18_result), .new_carry(subtractor_18_new_carry));
  or or_6 (or_6_out, subtractor_16_result, subtractor_15_result, subtractor_18_result, subtractor_17_result);
endmodule

module Subtractor (
  input  number_1,
  input  number_2,
  input  carry,
  output result,
  output new_carry
);

  wire and_1_out, and_2_out, and_3_out, xor_1_out;

  and and_1 (and_1_out, ~number_1, carry);  // AND_Gate
  and and_2 (and_2_out, ~number_1, number_2);  // AND_Gate
  or or_1 (new_carry, and_1_out, and_2_out, and_3_out);
  and and_3 (and_3_out, number_2, carry);
  xor xor_1 (xor_1_out, number_1, number_2);
  xor xor_2 (result, xor_1_out, carry);
endmodule

module Microprocessor (
  input  in_1,
  input  [17:0] in_2
);

  wire CF_out_4, clock_1_out, comparator_1_carry_flag, comparator_1_zero_flag, controller_1_data_memo_str,
       controller_1_flag_load, controller_1_ir_load, controller_1_memo_alu_mux, controller_1_pc_load,
       controller_1_rf_enable, controller_1_rf_init, controller_1_store_to_memo_mux, ZF_out_4;
  wire [2:0] controller_1_jump_select;
  wire [3:0] Inst_Register_out_4_2, multiplexer_1_out;
  wire [13:0] Inst_Register_out_4;
  wire [17:0] multiplexer_2_out, multiplexer_3_out, pc_1_new_pc, ram_1_data, Reg_File_data_to_read_1,
       Reg_File_data_to_read_2, rom_1_data, signextender6to18bits_1_output_extended_18bits;

  PC pc_1 (
    .immidiate(Inst_Register_out_4[9:0]), .current_address(pc_1_new_pc), .ZF(ZF_out_4), .CF(CF_out_4),
    .JUMP_slct(controller_1_jump_select), .clk(clock_1_out), .load(controller_1_pc_load), .new_PC(pc_1_new_pc));
  ROM #(.addrWidth(18), .dataWidth(18)) rom_1 (.addr(pc_1_new_pc), .data(rom_1_data), .sel(1'b1));
  Clock clock_1 (.out(clock_1_out));
  flag CF (.in_1(comparator_1_carry_flag), .load(controller_1_flag_load), .out_4(CF_out_4), .clk(clock_1_out));
  flag ZF (.in_1(comparator_1_zero_flag), .load(controller_1_flag_load), .out_4(ZF_out_4), .clk(clock_1_out));
  Controller controller_1 (
    .init(in_1), .opcode(Inst_Register_out_4_2), .clk(clock_1_out), .PC_load(controller_1_pc_load),
    .RF_init(controller_1_rf_init), .RF_enable(controller_1_rf_enable), .Flag_load(controller_1_flag_load),
    .memo_ALU_MUX(controller_1_memo_alu_mux), .store_to_memo_MUX(controller_1_store_to_memo_mux),
    .data_memo_str(controller_1_data_memo_str), .IR_load(controller_1_ir_load),
    .jump_select(controller_1_jump_select));
  Register_Parallel_Load Inst_Register (
    .in_1(rom_1_data), .load(controller_1_ir_load), .out_4({Inst_Register_out_4_2, Inst_Register_out_4}),
    .clk(clock_1_out));
  Comparator comparator_1 (
    .number_1(Reg_File_data_to_read_1), .number_2(Reg_File_data_to_read_2),
    .CARRY_FLAG(comparator_1_carry_flag), .ZERO_FLAG(comparator_1_zero_flag));
  Multiplexer #(.width(4), .enable("false")) multiplexer_1 (
    .in0(Inst_Register_out_4[9:6]), .in1(Inst_Register_out_4[13:10]), .out(multiplexer_1_out),
    .sel(controller_1_store_to_memo_mux));
  Multiplexer #(.width(18), .enable("false")) multiplexer_2 (
    .in0(ram_1_data), .in1(in_2), .out(multiplexer_2_out), .sel(controller_1_memo_alu_mux));
  Register_File_Initialised Reg_File (
    .Data_to_Write(multiplexer_2_out), .load(controller_1_rf_enable), .Reg_No(Inst_Register_out_4[13:10]),
    .enable(controller_1_rf_init), .Data_to_Read_1(Reg_File_data_to_read_1),
    .Data_to_Read_2(Reg_File_data_to_read_2), .Reg_No_1(multiplexer_1_out),
    .Reg_No_2(Inst_Register_out_4[3:0]), .clk(clock_1_out));
  RAM #(.addrWidth(10), .dataWidth(18), .bus("separate")) ram_1 (
    .addr(Inst_Register_out_4[9:0]), .din(Reg_File_data_to_read_1), .data(ram_1_data),
    .str(controller_1_data_memo_str), .sel(1'b1), .clk(clock_1_out), .ld(1'b1), .clr(1'b0));
  signExtender6To18bits signextender6to18bits_1 (
    .immediate(Inst_Register_out_4[5:0]),
    .output_extended_18bits(signextender6to18bits_1_output_extended_18bits));
  Multiplexer #(.width(18), .enable("false")) multiplexer_3 (
    .in0(Reg_File_data_to_read_2), .in1(signextender6to18bits_1_output_extended_18bits),
    .out(multiplexer_3_out), .sel(Inst_Register_out_4_2[2]));
  ALU alu_1 (
    .a(Reg_File_data_to_read_1), .b(multiplexer_3_out), .result(in_2),
    ._15th_14th_bit(Inst_Register_out_4_2[1:0]));  // open: carryOut

  // Notes on the sheet:
  //   INSTRUCTION MEMO
  //   contents of rom_1 (hex, n*v repeats v):
  //   187fe 840 1cff6 5001 1327b 9001 f909 243f2 4a05 283fc 2c303 3023a 343c1 383f1 20c09
  //   DR
  //   addr
  //   SR1
  //   imm
  //   SR2
  //   opcode
  //   store to memo
  //   DATA MEMO
endmodule

module Register_Parallel_Load (
  input  [17:0] in_1,
  input  load,
  input  clk,
  output [17:0] out_4
);

  wire [17:0] multiplexer_1_out;

  Multiplexer #(.width(18), .enable("false")) multiplexer_1 (
    .in0(out_4), .in1(in_1), .out(multiplexer_1_out), .sel(load));
  Register register_1 (.I(multiplexer_1_out), .clk(clk), .Q(out_4));  // open: initialise, load
endmodule

module Register_Multifunction (
  input  [17:0] in_1,
  input  [1:0] operation,
  input  clk,
  output [17:0] out_4
);

  wire [17:0] multiplexer_1_out;

  Multiplexer #(.select(2), .width(18), .enable("false")) multiplexer_1 (
    .in0({18{1'b0}}), .in1({18{1'b0}}), .in2(out_4), .in3(in_1), .out(multiplexer_1_out), .sel(operation));
  Register register_1 (.I(multiplexer_1_out), .clk(clk), .Q(out_4));  // open: initialise, load
endmodule

module Register_File (
  input  [17:0] Data_to_Write,
  input  enable_read,
  input  [3:0] Reg_No_1,
  input  [3:0] Reg_No_2,
  input  enable_write,
  input  [3:0] Reg_No,
  input  clk,
  output [17:0] Data_to_Read_1,
  output [17:0] Data_to_Read_2
);

  wire decoder_1_out0, decoder_1_out1, decoder_1_out2, decoder_1_out3, decoder_1_out4, decoder_1_out5,
       decoder_1_out6, decoder_1_out7, decoder_1_out8, decoder_1_out9, decoder_1_out10, decoder_1_out11,
       decoder_1_out12, decoder_1_out13, decoder_1_out14, decoder_1_out15;
  wire [17:0] register_parallel_load_1_out_4, register_parallel_load_2_out_4, register_parallel_load_3_out_4,
       register_parallel_load_4_out_4, register_parallel_load_5_out_4, register_parallel_load_6_out_4,
       register_parallel_load_7_out_4, register_parallel_load_8_out_4, register_parallel_load_9_out_4,
       register_parallel_load_10_out_4, register_parallel_load_11_out_4, register_parallel_load_12_out_4,
       register_parallel_load_13_out_4, register_parallel_load_14_out_4, register_parallel_load_15_out_4,
       register_parallel_load_16_out_4;

  Decoder #(.select(4)) decoder_1 (
    .out0(decoder_1_out0), .out1(decoder_1_out1), .out2(decoder_1_out2), .out3(decoder_1_out3),
    .out4(decoder_1_out4), .out5(decoder_1_out5), .out6(decoder_1_out6), .out7(decoder_1_out7),
    .out8(decoder_1_out8), .out9(decoder_1_out9), .out10(decoder_1_out10), .out11(decoder_1_out11),
    .out12(decoder_1_out12), .out13(decoder_1_out13), .out14(decoder_1_out14), .out15(decoder_1_out15),
    .sel(Reg_No), .en(enable_write));
  Register_Parallel_Load register_parallel_load_1 (
    .in_1(Data_to_Write), .load(decoder_1_out15), .out_4(register_parallel_load_1_out_4), .clk(clk));
  Register_Parallel_Load register_parallel_load_2 (
    .in_1(Data_to_Write), .load(decoder_1_out14), .out_4(register_parallel_load_2_out_4), .clk(clk));
  Register_Parallel_Load register_parallel_load_3 (
    .in_1(Data_to_Write), .load(decoder_1_out13), .out_4(register_parallel_load_3_out_4), .clk(clk));
  Register_Parallel_Load register_parallel_load_4 (
    .in_1(Data_to_Write), .load(decoder_1_out12), .out_4(register_parallel_load_4_out_4), .clk(clk));
  Register_Parallel_Load register_parallel_load_5 (
    .in_1(Data_to_Write), .load(decoder_1_out11), .out_4(register_parallel_load_5_out_4), .clk(clk));
  Register_Parallel_Load register_parallel_load_6 (
    .in_1(Data_to_Write), .load(decoder_1_out9), .out_4(register_parallel_load_6_out_4), .clk(clk));
  Register_Parallel_Load register_parallel_load_7 (
    .in_1(Data_to_Write), .load(decoder_1_out10), .out_4(register_parallel_load_7_out_4), .clk(clk));
  Register_Parallel_Load register_parallel_load_8 (
    .in_1(Data_to_Write), .load(decoder_1_out8), .out_4(register_parallel_load_8_out_4), .clk(clk));
  Register_Parallel_Load register_parallel_load_9 (
    .in_1(Data_to_Write), .load(decoder_1_out7), .out_4(register_parallel_load_9_out_4), .clk(clk));
  Register_Parallel_Load register_parallel_load_10 (
    .in_1(Data_to_Write), .load(decoder_1_out6), .out_4(register_parallel_load_10_out_4), .clk(clk));
  Register_Parallel_Load register_parallel_load_11 (
    .in_1(Data_to_Write), .load(decoder_1_out5), .out_4(register_parallel_load_11_out_4), .clk(clk));
  Register_Parallel_Load register_parallel_load_12 (
    .in_1(Data_to_Write), .load(decoder_1_out4), .out_4(register_parallel_load_12_out_4), .clk(clk));
  Register_Parallel_Load register_parallel_load_13 (
    .in_1(Data_to_Write), .load(decoder_1_out3), .out_4(register_parallel_load_13_out_4), .clk(clk));
  Register_Parallel_Load register_parallel_load_14 (
    .in_1(Data_to_Write), .load(decoder_1_out2), .out_4(register_parallel_load_14_out_4), .clk(clk));
  Register_Parallel_Load register_parallel_load_15 (
    .in_1(Data_to_Write), .load(decoder_1_out1), .out_4(register_parallel_load_15_out_4), .clk(clk));
  Register_Parallel_Load register_parallel_load_16 (
    .in_1(Data_to_Write), .load(decoder_1_out0), .out_4(register_parallel_load_16_out_4), .clk(clk));
  Multiplexer #(.select(4), .width(18)) multiplexer_1 (
    .in0(register_parallel_load_16_out_4), .in1(register_parallel_load_15_out_4),
    .in2(register_parallel_load_14_out_4), .in3(register_parallel_load_13_out_4),
    .in4(register_parallel_load_12_out_4), .in5(register_parallel_load_11_out_4),
    .in6(register_parallel_load_10_out_4), .in7(register_parallel_load_9_out_4),
    .in8(register_parallel_load_8_out_4), .in9(register_parallel_load_6_out_4),
    .in10(register_parallel_load_7_out_4), .in11(register_parallel_load_5_out_4),
    .in12(register_parallel_load_4_out_4), .in13(register_parallel_load_3_out_4),
    .in14(register_parallel_load_2_out_4), .in15(register_parallel_load_1_out_4), .out(Data_to_Read_1),
    .sel(Reg_No_1), .en(enable_read));
  Multiplexer #(.select(4), .width(18)) multiplexer_2 (
    .in0(register_parallel_load_16_out_4), .in1(register_parallel_load_15_out_4),
    .in2(register_parallel_load_14_out_4), .in3(register_parallel_load_13_out_4),
    .in4(register_parallel_load_12_out_4), .in5(register_parallel_load_11_out_4),
    .in6(register_parallel_load_10_out_4), .in7(register_parallel_load_9_out_4),
    .in8(register_parallel_load_8_out_4), .in9(register_parallel_load_6_out_4),
    .in10(register_parallel_load_7_out_4), .in11(register_parallel_load_5_out_4),
    .in12(register_parallel_load_4_out_4), .in13(register_parallel_load_3_out_4),
    .in14(register_parallel_load_2_out_4), .in15(register_parallel_load_1_out_4), .out(Data_to_Read_2),
    .sel(Reg_No_2), .en(enable_read));
endmodule

module Register_File_Initialised (
  input  [17:0] Data_to_Write,
  input  [3:0] Reg_No_1,
  input  [3:0] Reg_No_2,
  input  load,
  input  [3:0] Reg_No,
  input  enable,
  input  clk,
  output [17:0] Data_to_Read_1,
  output [17:0] Data_to_Read_2
);

  wire and_1_out, and_2_out, and_3_out, and_4_out, and_5_out, and_6_out, and_7_out, and_8_out, and_9_out,
       and_10_out, and_11_out, and_12_out, and_13_out, and_14_out, and_15_out, and_16_out, decoder_1_out0,
       decoder_1_out1, decoder_1_out2, decoder_1_out3, decoder_1_out4, decoder_1_out5, decoder_1_out6,
       decoder_1_out7, decoder_1_out8, decoder_1_out9, decoder_1_out10, decoder_1_out11, decoder_1_out12,
       decoder_1_out13, decoder_1_out14, decoder_1_out15, multiplexer_2_out, not_1_out, or_1_out, or_2_out,
       or_3_out, or_4_out, or_5_out, or_6_out, or_7_out, or_8_out, or_9_out, or_10_out, or_11_out, or_12_out,
       or_13_out, or_14_out, or_15_out, or_16_out;
  wire [17:0] multiplexer_1_out, register_parallel_load_1_out_4, register_parallel_load_2_out_4,
       register_parallel_load_3_out_4, register_parallel_load_4_out_4, register_parallel_load_5_out_4,
       register_parallel_load_6_out_4, register_parallel_load_7_out_4, register_parallel_load_8_out_4,
       register_parallel_load_9_out_4, register_parallel_load_10_out_4, register_parallel_load_11_out_4,
       register_parallel_load_12_out_4, register_parallel_load_13_out_4, register_parallel_load_14_out_4,
       register_parallel_load_15_out_4, register_parallel_load_16_out_4;

  Decoder #(.select(4)) decoder_1 (
    .out0(decoder_1_out0), .out1(decoder_1_out1), .out2(decoder_1_out2), .out3(decoder_1_out3),
    .out4(decoder_1_out4), .out5(decoder_1_out5), .out6(decoder_1_out6), .out7(decoder_1_out7),
    .out8(decoder_1_out8), .out9(decoder_1_out9), .out10(decoder_1_out10), .out11(decoder_1_out11),
    .out12(decoder_1_out12), .out13(decoder_1_out13), .out14(decoder_1_out14), .out15(decoder_1_out15),
    .sel(Reg_No), .en(load));
  not not_1 (not_1_out, enable);
  Multiplexer #(.width(18), .enable("false")) multiplexer_1 (
    .in0(Data_to_Write), .in1({18{1'b0}}), .out(multiplexer_1_out), .sel(not_1_out));
  Multiplexer #(.enable("false")) multiplexer_2 (.in0(load), .in1(not_1_out), .out(multiplexer_2_out), .sel(not_1_out));
  Register_Parallel_Load register_parallel_load_1 (
    .in_1(multiplexer_1_out), .load(and_1_out), .out_4(register_parallel_load_1_out_4), .clk(clk));
  and and_1 (and_1_out, multiplexer_2_out, or_1_out);
  or or_1 (or_1_out, decoder_1_out15, not_1_out);
  Register_Parallel_Load register_parallel_load_2 (
    .in_1(multiplexer_1_out), .load(and_2_out), .out_4(register_parallel_load_2_out_4), .clk(clk));
  and and_2 (and_2_out, multiplexer_2_out, or_2_out);
  or or_2 (or_2_out, decoder_1_out14, not_1_out);
  Register_Parallel_Load register_parallel_load_3 (
    .in_1(multiplexer_1_out), .load(and_3_out), .out_4(register_parallel_load_3_out_4), .clk(clk));
  and and_3 (and_3_out, multiplexer_2_out, or_3_out);
  or or_3 (or_3_out, decoder_1_out13, not_1_out);
  Register_Parallel_Load register_parallel_load_4 (
    .in_1(multiplexer_1_out), .load(and_4_out), .out_4(register_parallel_load_4_out_4), .clk(clk));
  and and_4 (and_4_out, multiplexer_2_out, or_4_out);
  or or_4 (or_4_out, decoder_1_out12, not_1_out);
  Register_Parallel_Load register_parallel_load_5 (
    .in_1(multiplexer_1_out), .load(and_5_out), .out_4(register_parallel_load_5_out_4), .clk(clk));
  and and_5 (and_5_out, multiplexer_2_out, or_5_out);
  or or_5 (or_5_out, decoder_1_out11, not_1_out);
  Register_Parallel_Load register_parallel_load_6 (
    .in_1(multiplexer_1_out), .load(and_6_out), .out_4(register_parallel_load_6_out_4), .clk(clk));
  Register_Parallel_Load register_parallel_load_7 (
    .in_1(multiplexer_1_out), .load(and_7_out), .out_4(register_parallel_load_7_out_4), .clk(clk));
  and and_6 (and_6_out, multiplexer_2_out, or_6_out);
  and and_7 (and_7_out, multiplexer_2_out, or_7_out);
  or or_6 (or_6_out, decoder_1_out9, not_1_out);
  or or_7 (or_7_out, decoder_1_out10, not_1_out);
  Register_Parallel_Load register_parallel_load_8 (
    .in_1(multiplexer_1_out), .load(and_8_out), .out_4(register_parallel_load_8_out_4), .clk(clk));
  and and_8 (and_8_out, multiplexer_2_out, or_8_out);
  or or_8 (or_8_out, decoder_1_out8, not_1_out);
  Register_Parallel_Load register_parallel_load_9 (
    .in_1(multiplexer_1_out), .load(and_9_out), .out_4(register_parallel_load_9_out_4), .clk(clk));
  and and_9 (and_9_out, multiplexer_2_out, or_9_out);
  or or_9 (or_9_out, decoder_1_out7, not_1_out);
  Register_Parallel_Load register_parallel_load_10 (
    .in_1(multiplexer_1_out), .load(and_10_out), .out_4(register_parallel_load_10_out_4), .clk(clk));
  and and_10 (and_10_out, multiplexer_2_out, or_10_out);
  or or_10 (or_10_out, decoder_1_out6, not_1_out);
  Register_Parallel_Load register_parallel_load_11 (
    .in_1(multiplexer_1_out), .load(and_11_out), .out_4(register_parallel_load_11_out_4), .clk(clk));
  and and_11 (and_11_out, multiplexer_2_out, or_11_out);
  or or_11 (or_11_out, decoder_1_out5, not_1_out);
  Register_Parallel_Load register_parallel_load_12 (
    .in_1(multiplexer_1_out), .load(and_13_out), .out_4(register_parallel_load_12_out_4), .clk(clk));
  and and_12 (and_12_out, multiplexer_2_out, or_14_out);
  and and_13 (and_13_out, multiplexer_2_out, or_12_out);
  or or_12 (or_12_out, decoder_1_out4, not_1_out);
  Register_Parallel_Load register_parallel_load_13 (
    .in_1(multiplexer_1_out), .load(and_12_out), .out_4(register_parallel_load_13_out_4), .clk(clk));
  Register_Parallel_Load register_parallel_load_14 (
    .in_1(multiplexer_1_out), .load(and_14_out), .out_4(register_parallel_load_14_out_4), .clk(clk));
  and and_14 (and_14_out, multiplexer_2_out, or_13_out);
  or or_13 (or_13_out, decoder_1_out2, not_1_out);
  or or_14 (or_14_out, decoder_1_out3, not_1_out);
  Register_Parallel_Load register_parallel_load_15 (
    .in_1(multiplexer_1_out), .load(and_15_out), .out_4(register_parallel_load_15_out_4), .clk(clk));
  and and_15 (and_15_out, multiplexer_2_out, or_15_out);
  or or_15 (or_15_out, decoder_1_out1, not_1_out);
  Register_Parallel_Load register_parallel_load_16 (
    .in_1(multiplexer_1_out), .load(and_16_out), .out_4(register_parallel_load_16_out_4), .clk(clk));
  and and_16 (and_16_out, multiplexer_2_out, or_16_out);
  or or_16 (or_16_out, decoder_1_out0, not_1_out);
  Multiplexer #(.select(4), .width(18), .enable("false")) multiplexer_3 (
    .in0(register_parallel_load_16_out_4), .in1(register_parallel_load_15_out_4),
    .in2(register_parallel_load_14_out_4), .in3(register_parallel_load_13_out_4),
    .in4(register_parallel_load_12_out_4), .in5(register_parallel_load_11_out_4),
    .in6(register_parallel_load_10_out_4), .in7(register_parallel_load_9_out_4),
    .in8(register_parallel_load_8_out_4), .in9(register_parallel_load_6_out_4),
    .in10(register_parallel_load_7_out_4), .in11(register_parallel_load_5_out_4),
    .in12(register_parallel_load_4_out_4), .in13(register_parallel_load_3_out_4),
    .in14(register_parallel_load_2_out_4), .in15(register_parallel_load_1_out_4), .out(Data_to_Read_1),
    .sel(Reg_No_1));
  Multiplexer #(.select(4), .width(18), .enable("false")) multiplexer_4 (
    .in0(register_parallel_load_16_out_4), .in1(register_parallel_load_15_out_4),
    .in2(register_parallel_load_14_out_4), .in3(register_parallel_load_13_out_4),
    .in4(register_parallel_load_12_out_4), .in5(register_parallel_load_11_out_4),
    .in6(register_parallel_load_10_out_4), .in7(register_parallel_load_9_out_4),
    .in8(register_parallel_load_8_out_4), .in9(register_parallel_load_6_out_4),
    .in10(register_parallel_load_7_out_4), .in11(register_parallel_load_5_out_4),
    .in12(register_parallel_load_4_out_4), .in13(register_parallel_load_3_out_4),
    .in14(register_parallel_load_2_out_4), .in15(register_parallel_load_1_out_4), .out(Data_to_Read_2),
    .sel(Reg_No_2));
endmodule

module FullAdder1bit (
  input  a,
  input  b,
  input  carryIn,
  output carryOut,
  output sum
);

  wire and_1_out, and_2_out, and_3_out;

  and and_1 (and_1_out, a, b);
  and and_2 (and_2_out, b, carryIn);
  and and_3 (and_3_out, a, carryIn);
  xor xor_1 (sum, a, b, carryIn);
  or or_1 (carryOut, and_1_out, and_2_out, and_3_out);
endmodule

module HalfAdder (
  input  a,
  input  b,
  output sum,
  output carryout
);

  xor xor_1 (sum, a, b);
  and and_1 (carryout, a, b);
endmodule

module _2BitAdder (
  input  [1:0] a,
  input  [1:0] b,
  input  carryIn,
  output [1:0] sum,
  output carryOut
);

  wire fulladder1bit_1_carryout;

  FullAdder1bit fulladder1bit_1 (
    .a(a[0]), .b(b[0]), .carryIn(carryIn), .carryOut(fulladder1bit_1_carryout), .sum(sum[0]));
  FullAdder1bit fulladder1bit_2 (
    .a(a[1]), .b(b[1]), .carryIn(fulladder1bit_1_carryout), .carryOut(carryOut), .sum(sum[1]));

  // Notes on the sheet:
  //   2-Bit Adder
endmodule

module _18bitadder (
  input  carryIn,
  input  [17:0] operand_1,
  input  [17:0] operand_2,
  output [17:0] sum,
  output carryOut
);

  wire n2bitadder_1_carryout, n2bitadder_2_carryout, n2bitadder_3_carryout, n2bitadder_4_carryout,
       n2bitadder_5_carryout, n2bitadder_6_carryout, n2bitadder_7_carryout, n2bitadder_8_carryout;

  _2BitAdder u_2bitadder_1 (
    .a(operand_1[1:0]), .b(operand_2[1:0]), .carryIn(carryIn), .sum(sum[1:0]),
    .carryOut(n2bitadder_1_carryout));
  _2BitAdder u_2bitadder_2 (
    .a(operand_1[3:2]), .b(operand_2[3:2]), .carryIn(n2bitadder_1_carryout), .sum(sum[3:2]),
    .carryOut(n2bitadder_2_carryout));
  _2BitAdder u_2bitadder_3 (
    .a(operand_1[5:4]), .b(operand_2[5:4]), .carryIn(n2bitadder_2_carryout), .sum(sum[5:4]),
    .carryOut(n2bitadder_3_carryout));
  _2BitAdder u_2bitadder_4 (
    .a(operand_1[7:6]), .b(operand_2[7:6]), .carryIn(n2bitadder_3_carryout), .sum(sum[7:6]),
    .carryOut(n2bitadder_4_carryout));
  _2BitAdder u_2bitadder_5 (
    .a(operand_2[9:8]), .b(operand_1[9:8]), .carryIn(n2bitadder_4_carryout), .sum(sum[9:8]),
    .carryOut(n2bitadder_5_carryout));
  _2BitAdder u_2bitadder_6 (
    .a(operand_1[11:10]), .b(operand_2[11:10]), .carryIn(n2bitadder_5_carryout), .sum(sum[11:10]),
    .carryOut(n2bitadder_6_carryout));
  _2BitAdder u_2bitadder_7 (
    .a(operand_1[13:12]), .b(operand_2[13:12]), .carryIn(n2bitadder_6_carryout), .sum(sum[13:12]),
    .carryOut(n2bitadder_7_carryout));
  _2BitAdder u_2bitadder_8 (
    .a(operand_1[15:14]), .b(operand_2[15:14]), .carryIn(n2bitadder_7_carryout), .sum(sum[15:14]),
    .carryOut(n2bitadder_8_carryout));
  _2BitAdder u_2bitadder_9 (
    .a(operand_1[17:16]), .b(operand_2[17:16]), .carryIn(n2bitadder_8_carryout), .sum(sum[17:16]),
    .carryOut(carryOut));
endmodule

// Ext
module signExtender6To18bits (
  input  [5:0] immediate,
  output [17:0] output_extended_18bits
);


  assign output_extended_18bits = {{13{immediate[5]}}, immediate[4:0]};
endmodule

// Ext
module signExtention4To18Bits (
  input  [3:0] register,
  output [17:0] output_extended_18bits
);


  assign output_extended_18bits = {{15{register[3]}}, register[2:0]};
endmodule

module signExtention10To18Bits (
  input  [9:0] immediate,
  output [17:0] output_extended_18bits
);


  assign output_extended_18bits = {{9{immediate[9]}}, immediate[8:0]};
endmodule

module PC (
  input  [9:0] immidiate,
  input  [17:0] current_address,
  input  [2:0] JUMP_slct,
  input  clk,
  input  load,
  input  ZF,
  input  CF,
  output [17:0] new_PC
);

  wire [17:0] bit_extender_1_out, multiplexer_1_out, multiplexer_2_out, multiplexer_3_out, multiplexer_4_out,
       multiplexer_5_out, multiplexer_6_out, multiplexer_7_out, multiplexer_8_out, multiplexer_9_out,
       multiplexer_10_out, PC_imm_sum, PC_plus_plus_sum;

  assign bit_extender_1_out = {{8{1'b0}}, immidiate};  // Bit_Extender bit_extender_1
  Adder18Bits PC_imm (.operand_1(bit_extender_1_out), .operand_2(current_address), .sum(PC_imm_sum));  // open: carryOut
  Adder18Bits PC_plus_plus (.operand_1(current_address), .operand_2(18'h1), .sum(PC_plus_plus_sum));  // open: carryOut
  Multiplexer #(.width(18), .enable("false")) multiplexer_1 (
    .in0(PC_plus_plus_sum), .in1(PC_imm_sum), .out(multiplexer_1_out), .sel(ZF));
  Multiplexer #(.width(18), .enable("false")) multiplexer_2 (
    .in0(PC_imm_sum), .in1(PC_plus_plus_sum), .out(multiplexer_2_out), .sel(ZF));
  Multiplexer #(.width(18), .enable("false")) multiplexer_3 (
    .in0(PC_imm_sum), .in1(PC_plus_plus_sum), .out(multiplexer_3_out), .sel(ZF));
  Multiplexer #(.width(18), .enable("false")) multiplexer_4 (
    .in0(PC_plus_plus_sum), .in1(PC_imm_sum), .out(multiplexer_4_out), .sel(ZF));
  Multiplexer #(.width(18), .enable("false")) multiplexer_5 (
    .in0(multiplexer_1_out), .in1(PC_plus_plus_sum), .out(multiplexer_5_out), .sel(CF));
  Multiplexer #(.width(18), .enable("false")) multiplexer_6 (
    .in0(multiplexer_2_out), .in1(PC_plus_plus_sum), .out(multiplexer_6_out), .sel(CF));
  Multiplexer #(.width(18), .enable("false")) multiplexer_7 (
    .in0(PC_plus_plus_sum), .in1(multiplexer_3_out), .out(multiplexer_7_out), .sel(CF));
  Multiplexer #(.width(18), .enable("false")) multiplexer_8 (
    .in0(PC_imm_sum), .in1(PC_plus_plus_sum), .out(multiplexer_8_out), .sel(CF));
  Multiplexer #(.width(18), .enable("false")) multiplexer_9 (
    .in0(PC_plus_plus_sum), .in1(multiplexer_4_out), .out(multiplexer_9_out), .sel(CF));
  Multiplexer #(.select(3), .width(18), .enable("false")) multiplexer_10 (
    .in0({18{1'b0}}), .in1(PC_imm_sum), .in2(multiplexer_5_out), .in3(multiplexer_6_out),
    .in4(multiplexer_7_out), .in5(multiplexer_8_out), .in6(multiplexer_9_out), .in7(PC_plus_plus_sum),
    .out(multiplexer_10_out), .sel(JUMP_slct));
  Register_Parallel_Load register_parallel_load_1 (.in_1(multiplexer_10_out), .load(load), .out_4(new_PC), .clk(clk));
endmodule

module Adder18Bits (
  input  [17:0] operand_1,
  input  [17:0] operand_2,
  output [17:0] sum,
  output carryOut
);

  wire n2bitadder_1_carryout, n2bitadder_2_carryout, n2bitadder_3_carryout, n2bitadder_4_carryout,
       n2bitadder_5_carryout, n2bitadder_6_carryout, n2bitadder_7_carryout, n2bitadder_8_carryout;

  _2BitAdder u_2bitadder_1 (
    .a(operand_1[1:0]), .b(operand_2[1:0]), .carryIn(1'b0), .sum(sum[1:0]), .carryOut(n2bitadder_1_carryout));
  _2BitAdder u_2bitadder_2 (
    .a(operand_1[3:2]), .b(operand_2[3:2]), .carryIn(n2bitadder_1_carryout), .sum(sum[3:2]),
    .carryOut(n2bitadder_2_carryout));
  _2BitAdder u_2bitadder_3 (
    .a(operand_1[5:4]), .b(operand_2[5:4]), .carryIn(n2bitadder_2_carryout), .sum(sum[5:4]),
    .carryOut(n2bitadder_3_carryout));
  _2BitAdder u_2bitadder_4 (
    .a(operand_1[7:6]), .b(operand_2[7:6]), .carryIn(n2bitadder_3_carryout), .sum(sum[7:6]),
    .carryOut(n2bitadder_4_carryout));
  _2BitAdder u_2bitadder_5 (
    .a(operand_2[9:8]), .b(operand_1[9:8]), .carryIn(n2bitadder_4_carryout), .sum(sum[9:8]),
    .carryOut(n2bitadder_5_carryout));
  _2BitAdder u_2bitadder_6 (
    .a(operand_1[11:10]), .b(operand_2[11:10]), .carryIn(n2bitadder_5_carryout), .sum(sum[11:10]),
    .carryOut(n2bitadder_6_carryout));
  _2BitAdder u_2bitadder_7 (
    .a(operand_1[13:12]), .b(operand_2[13:12]), .carryIn(n2bitadder_6_carryout), .sum(sum[13:12]),
    .carryOut(n2bitadder_7_carryout));
  _2BitAdder u_2bitadder_8 (
    .a(operand_1[15:14]), .b(operand_2[15:14]), .carryIn(n2bitadder_7_carryout), .sum(sum[15:14]),
    .carryOut(n2bitadder_8_carryout));
  _2BitAdder u_2bitadder_9 (
    .a(operand_1[17:16]), .b(operand_2[17:16]), .carryIn(n2bitadder_8_carryout), .sum(sum[17:16]),
    .carryOut(carryOut));
endmodule

module ALU (
  input  [17:0] a,
  input  [17:0] b,
  input  [1:0] _15th_14th_bit,
  output carryOut,
  output [17:0] result
);

  wire [17:0] adder18bits_1_sum, and_1_out, nand_1_out, nor_1_out;

  Adder18Bits adder18bits_1 (.operand_1(a), .operand_2(b), .carryOut(carryOut), .sum(adder18bits_1_sum));
  assign and_1_out = a & b;  // AND_Gate and_1, 18 bits wide
  assign nand_1_out = ~(a & b);  // NAND_Gate nand_1, 18 bits wide
  assign nor_1_out = ~(a | b);  // NOR_Gate nor_1, 18 bits wide
  Multiplexer #(.select(2), .width(18), .enable("false")) multiplexer_1 (
    .in0(adder18bits_1_sum), .in1(and_1_out), .in2(nand_1_out), .in3(nor_1_out), .out(result),
    .sel(_15th_14th_bit));
endmodule

module flag (
  input  in_1,
  input  load,
  input  clk,
  output out_4
);

  wire multiplexer_1_out;

  Multiplexer #(.enable("false")) multiplexer_1 (.in0(out_4), .in1(in_1), .out(multiplexer_1_out), .sel(load));
  D_Flip_Flop d_flip_flop_1 (.D(multiplexer_1_out), .Q(out_4), .Clk(clk));
endmodule

module Controller_Combinational_Logic (
  input  [2:0] state,
  input  [3:0] opcode,
  output [2:0] next_state,
  output PC_load,
  output RF_init,
  output RF_enable,
  output Flag_load,
  output memo_ALU_MUX,
  output store_to_memo_MUX,
  output data_memo_str,
  output IR_load,
  output [2:0] jump_select
);

  wire and_1_out, and_2_out, and_3_out, and_4_out, and_5_out, and_6_out, and_7_out, and_8_out, and_9_out,
       and_10_out, and_11_out, and_12_out, and_13_out, and_14_out, and_16_out, and_17_out, and_18_out,
       and_19_out, and_24_out, and_25_out, and_26_out, and_27_out, and_28_out, and_29_out, and_30_out,
       and_31_out, and_32_out, and_33_out, and_34_out, and_35_out, and_36_out, not_1_out, not_2_out,
       not_3_out, not_4_out, not_5_out, not_6_out, not_7_out, not_8_out, not_9_out, not_10_out, not_11_out,
       not_12_out, not_13_out, not_14_out, not_15_out, not_16_out, not_17_out, not_18_out, not_19_out,
       not_20_out, not_21_out, not_22_out, not_23_out, not_24_out, not_25_out, not_26_out, not_27_out,
       not_28_out, not_29_out, not_30_out, not_31_out, not_32_out, not_33_out, not_34_out, not_35_out,
       not_36_out, not_37_out, not_38_out, not_39_out, not_40_out, not_41_out, not_42_out, not_43_out,
       not_44_out, not_45_out, not_46_out, not_47_out, not_48_out, not_49_out, not_50_out;

  not not_1 (not_1_out, state[2]);
  not not_2 (not_2_out, state[0]);
  not not_3 (not_3_out, state[2]);
  not not_4 (not_4_out, state[0]);
  not not_5 (not_5_out, state[2]);
  not not_6 (not_6_out, state[1]);
  not not_7 (not_7_out, state[2]);
  not not_8 (not_8_out, state[0]);
  not not_9 (not_9_out, opcode[2]);
  not not_10 (not_10_out, state[2]);
  not not_11 (not_11_out, state[0]);
  not not_12 (not_12_out, opcode[1]);
  not not_13 (not_13_out, state[2]);
  not not_14 (not_14_out, state[0]);
  not not_15 (not_15_out, state[1]);
  not not_16 (not_16_out, state[0]);
  not not_17 (not_17_out, state[0]);
  not not_18 (not_18_out, opcode[3]);
  not not_19 (not_19_out, opcode[2]);
  not not_20 (not_20_out, state[0]);
  not not_21 (not_21_out, state[0]);
  not not_22 (not_22_out, opcode[1]);
  not not_23 (not_23_out, state[0]);
  not not_24 (not_24_out, state[1]);
  not not_25 (not_25_out, state[0]);
  not not_26 (not_26_out, state[2]);
  not not_27 (not_27_out, state[1]);
  not not_28 (not_28_out, state[0]);
  not not_29 (not_29_out, state[2]);
  not not_30 (not_30_out, state[1]);
  not not_31 (not_31_out, state[0]);
  not not_32 (not_32_out, state[2]);
  not not_33 (not_33_out, state[1]);
  not not_34 (not_34_out, state[0]);
  not not_35 (not_35_out, state[0]);
  not not_36 (not_36_out, state[2]);
  not not_37 (not_37_out, state[1]);
  not not_38 (not_38_out, state[1]);
  not not_39 (not_39_out, state[2]);
  not not_40 (not_40_out, state[1]);
  not not_41 (not_41_out, opcode[3]);
  not not_42 (not_42_out, state[2]);
  not not_43 (not_43_out, state[1]);
  not not_44 (not_44_out, state[0]);
  not not_45 (not_45_out, state[2]);
  not not_46 (not_46_out, state[1]);
  not not_47 (not_47_out, state[0]);
  not not_48 (not_48_out, state[2]);
  not not_49 (not_49_out, state[1]);
  not not_50 (not_50_out, state[0]);
  and and_1 (and_1_out, not_1_out, state[1], not_2_out, opcode[2], opcode[1]);
  and and_2 (and_2_out, not_3_out, state[1], not_4_out, opcode[3]);
  and and_3 (and_3_out, not_5_out, not_6_out, state[0]);
  and and_4 (and_4_out, not_7_out, state[1], not_8_out, not_9_out);
  and and_5 (and_5_out, not_10_out, state[1], not_11_out, not_12_out);
  and and_6 (and_6_out, not_13_out, state[1], not_14_out, opcode[3]);
  and and_7 (and_7_out, not_15_out, not_16_out);
  and and_8 (and_8_out, not_17_out, not_18_out, not_19_out);
  and and_9 (and_9_out, not_20_out, opcode[0]);
  and and_10 (and_10_out, not_21_out, opcode[2], not_22_out);
  and and_11 (and_11_out, not_23_out, opcode[3], opcode[1]);
  and and_12 (and_12_out, state[1], state[0]);
  and and_13 (and_13_out, not_24_out, not_25_out);
  and and_14 (and_14_out, state[1], state[0]);
  and and_15 (RF_init, not_26_out, not_27_out, not_28_out);
  and and_16 (and_16_out, not_29_out, state[1], state[0]);
  and and_17 (and_17_out, state[2], not_30_out, not_31_out);
  and and_18 (and_18_out, not_32_out, not_33_out, not_34_out);
  and and_19 (and_19_out, state[2], state[1], not_35_out);
  and and_20 (memo_ALU_MUX, not_36_out, state[1], state[0]);
  and and_21 (store_to_memo_MUX, state[2], not_37_out, state[0]);
  and and_22 (data_memo_str, state[2], not_38_out, state[0]);
  and and_23 (IR_load, not_39_out, not_40_out, state[0]);
  and and_24 (and_24_out, state[0], not_41_out);
  and and_25 (and_25_out, state[0], opcode[2]);
  and and_26 (and_26_out, not_42_out, state[1]);
  and and_27 (and_27_out, state[2], not_43_out);
  and and_28 (and_28_out, state[2], not_44_out);
  and and_29 (and_29_out, not_45_out, state[1]);
  and and_30 (and_30_out, state[1], opcode[1]);
  and and_31 (and_31_out, state[2], not_46_out);
  and and_32 (and_32_out, state[2], not_47_out);
  and and_33 (and_33_out, not_48_out, state[1]);
  and and_34 (and_34_out, state[1], opcode[0]);
  and and_35 (and_35_out, state[2], not_49_out);
  and and_36 (and_36_out, state[2], not_50_out);
  or or_1 (next_state[2], and_1_out, and_2_out);
  or or_2 (next_state[1], and_3_out, and_4_out, and_5_out, and_6_out);
  or or_3 (next_state[0], and_7_out, and_8_out, and_9_out, and_10_out, and_11_out, and_12_out, state[2]);
  or or_4 (PC_load, and_13_out, and_14_out, state[2]);
  or or_5 (RF_enable, and_16_out, and_17_out);
  or or_6 (Flag_load, and_18_out, and_19_out);
  or or_7 (jump_select[2], and_24_out, and_25_out, and_26_out, and_27_out, and_28_out);
  or or_8 (jump_select[1], and_29_out, and_30_out, and_31_out, and_32_out);
  or or_9 (jump_select[0], and_33_out, and_34_out, and_35_out, and_36_out);
endmodule

module controller_next_state (
  input  s2,
  input  s1,
  input  s0,
  input  op3,
  input  op2,
  input  op1,
  input  op0,
  output n2,
  output n1,
  output n0
);

  wire and_1_out, and_2_out, and_3_out, and_4_out, and_5_out, and_6_out, and_7_out, and_8_out, and_9_out,
       and_10_out, and_11_out, and_12_out, not_1_out, not_2_out, not_3_out, not_4_out, not_5_out, not_6_out,
       not_7_out, not_8_out, not_9_out, not_10_out, not_11_out, not_12_out, not_13_out, not_14_out,
       not_15_out, not_16_out, not_17_out, not_18_out, not_19_out, not_20_out, not_21_out, not_22_out,
       not_23_out;

  not not_1 (not_1_out, s2);
  not not_2 (not_2_out, s0);
  not not_3 (not_3_out, s2);
  not not_4 (not_4_out, s0);
  not not_5 (not_5_out, s2);
  not not_6 (not_6_out, s1);
  not not_7 (not_7_out, s2);
  not not_8 (not_8_out, s0);
  not not_9 (not_9_out, op2);
  not not_10 (not_10_out, s2);
  not not_11 (not_11_out, s0);
  not not_12 (not_12_out, op1);
  not not_13 (not_13_out, s2);
  not not_14 (not_14_out, s0);
  not not_15 (not_15_out, s1);
  not not_16 (not_16_out, s0);
  not not_17 (not_17_out, s0);
  not not_18 (not_18_out, op3);
  not not_19 (not_19_out, op2);
  not not_20 (not_20_out, s0);
  not not_21 (not_21_out, s0);
  not not_22 (not_22_out, op1);
  not not_23 (not_23_out, s0);
  and and_1 (and_1_out, not_1_out, s1, not_2_out, op2, op1);
  and and_2 (and_2_out, not_3_out, s1, not_4_out, op3);
  and and_3 (and_3_out, not_5_out, not_6_out, s0);
  and and_4 (and_4_out, not_7_out, s1, not_8_out, not_9_out);
  and and_5 (and_5_out, not_10_out, s1, not_11_out, not_12_out);
  and and_6 (and_6_out, not_13_out, s1, not_14_out, op3);
  and and_7 (and_7_out, not_15_out, not_16_out);
  and and_8 (and_8_out, not_17_out, not_18_out, not_19_out);
  and and_9 (and_9_out, not_20_out, op0);
  and and_10 (and_10_out, not_21_out, op2, not_22_out);
  and and_11 (and_11_out, not_23_out, op3, op1);
  and and_12 (and_12_out, s1, s0);
  or or_1 (n2, and_1_out, and_2_out);
  or or_2 (n1, and_3_out, and_4_out, and_5_out, and_6_out);
  or or_3 (n0, and_7_out, and_8_out, and_9_out, and_10_out, and_11_out, and_12_out, s2);
endmodule

module controller_outputs (
  input  s2,
  input  s1,
  input  s0,
  output PC_load,
  output RF_init,
  output RF_enable,
  output Flag_load,
  output memo_ALU_MUX,
  output store_to_memo_MUX,
  output data_memo_str,
  output IR_load,
  output JMP_slct_2,
  output JMP_slct_1,
  output JMP_slct_0
);

  wire and_1_out, and_2_out, and_3_out, and_4_out, and_5_out, and_7_out, and_8_out, and_9_out, and_10_out,
       not_1_out, not_2_out, not_3_out, not_4_out, not_5_out, not_6_out, not_7_out, not_8_out, not_9_out,
       not_10_out, not_11_out, not_12_out, not_13_out, not_14_out, not_15_out, not_16_out, not_17_out;

  not not_1 (not_1_out, s1);
  not not_2 (not_2_out, s0);
  not not_3 (not_3_out, s2);
  not not_4 (not_4_out, s1);
  not not_5 (not_5_out, s0);
  not not_6 (not_6_out, s2);
  not not_7 (not_7_out, s1);
  not not_8 (not_8_out, s0);
  not not_9 (not_9_out, s2);
  not not_10 (not_10_out, s1);
  not not_11 (not_11_out, s0);
  not not_12 (not_12_out, s0);
  not not_13 (not_13_out, s2);
  not not_14 (not_14_out, s1);
  not not_15 (not_15_out, s1);
  not not_16 (not_16_out, s2);
  not not_17 (not_17_out, s1);
  and and_1 (and_1_out, s1, s0);
  and and_2 (and_2_out, s1, s0);
  and and_3 (and_3_out, s1, s0);
  and and_4 (and_4_out, not_1_out, not_2_out);
  and and_5 (and_5_out, s1, s0);
  and and_6 (RF_init, not_3_out, not_4_out, not_5_out);
  and and_7 (and_7_out, not_6_out, s1, s0);
  and and_8 (and_8_out, s2, not_7_out, not_8_out);
  and and_9 (and_9_out, not_9_out, not_10_out, not_11_out);
  and and_10 (and_10_out, s2, s1, not_12_out);
  and and_11 (memo_ALU_MUX, not_13_out, s1, s0);
  and and_12 (store_to_memo_MUX, s2, not_14_out, s0);
  and and_13 (data_memo_str, s2, not_15_out, s0);
  and and_14 (IR_load, not_16_out, not_17_out, s0);
  or or_1 (JMP_slct_2, and_1_out, s2);
  or or_2 (JMP_slct_1, and_2_out, s2);
  or or_3 (JMP_slct_0, and_3_out, s2);
  or or_4 (PC_load, and_4_out, and_5_out, s2);
  or or_5 (RF_enable, and_7_out, and_8_out);
  or or_6 (Flag_load, and_9_out, and_10_out);
endmodule

module controller_jump_slct (
  input  s2,
  input  s1,
  input  s0,
  input  op3,
  input  op2,
  input  op1,
  input  op0,
  output JMP_slct_2,
  output JMP_slct_1,
  output JMP_slct_0
);

  wire and_1_out, and_2_out, and_3_out, and_4_out, and_5_out, and_6_out, and_7_out, and_8_out, and_9_out,
       and_10_out, and_11_out, and_12_out, and_13_out, not_1_out, not_2_out, not_3_out, not_4_out, not_5_out,
       not_6_out, not_7_out, not_8_out, not_9_out, not_10_out;

  not not_1 (not_1_out, op3);
  not not_2 (not_2_out, s2);
  not not_3 (not_3_out, s1);
  not not_4 (not_4_out, s0);
  not not_5 (not_5_out, s2);
  not not_6 (not_6_out, s1);
  not not_7 (not_7_out, s0);
  not not_8 (not_8_out, s2);
  not not_9 (not_9_out, s1);
  not not_10 (not_10_out, s0);
  and and_1 (and_1_out, s0, not_1_out);
  and and_2 (and_2_out, s0, op2);
  and and_3 (and_3_out, not_2_out, s1);
  and and_4 (and_4_out, s2, not_3_out);
  and and_5 (and_5_out, s2, not_4_out);
  and and_6 (and_6_out, not_5_out, s1);
  and and_7 (and_7_out, s1, op1);
  and and_8 (and_8_out, s2, not_6_out);
  and and_9 (and_9_out, s2, not_7_out);
  and and_10 (and_10_out, not_8_out, s1);
  and and_11 (and_11_out, s1, op0);
  and and_12 (and_12_out, s2, not_9_out);
  and and_13 (and_13_out, s2, not_10_out);
  or or_1 (JMP_slct_2, and_1_out, and_2_out, and_3_out, and_4_out, and_5_out);
  or or_2 (JMP_slct_1, and_6_out, and_7_out, and_8_out, and_9_out);
  or or_3 (JMP_slct_0, and_10_out, and_11_out, and_12_out, and_13_out);
endmodule

module Controller (
  input  init,
  input  [3:0] opcode,
  input  clk,
  output PC_load,
  output RF_init,
  output RF_enable,
  output Flag_load,
  output memo_ALU_MUX,
  output store_to_memo_MUX,
  output data_memo_str,
  output IR_load,
  output [2:0] jump_select
);

  wire [2:0] controller_combinational_logic_1_next_state, Register_q;

  Controller_Register Register (
    .I(controller_combinational_logic_1_next_state), .clk(clk), .enable(init), .Q(Register_q));
  Controller_Combinational_Logic controller_combinational_logic_1 (
    .state(Register_q), .opcode(opcode), .next_state(controller_combinational_logic_1_next_state),
    .PC_load(PC_load), .RF_init(RF_init), .RF_enable(RF_enable), .Flag_load(Flag_load),
    .memo_ALU_MUX(memo_ALU_MUX), .store_to_memo_MUX(store_to_memo_MUX), .data_memo_str(data_memo_str),
    .IR_load(IR_load), .jump_select(jump_select));
endmodule

module Controller_Register (
  input  [2:0] I,
  input  clk,
  input  enable,
  output [2:0] Q
);

  wire [2:0] d_flip_flop_3_q;

  D_Flip_Flop d_flip_flop_1 (.D(I[2]), .Q(d_flip_flop_3_q[2]), .Clk(clk));
  D_Flip_Flop d_flip_flop_2 (.D(I[1]), .Q(d_flip_flop_3_q[1]), .Clk(clk));
  D_Flip_Flop d_flip_flop_3 (.D(I[0]), .Q(d_flip_flop_3_q[0]), .Clk(clk));
  Multiplexer #(.width(3), .enable("false")) multiplexer_1 (.in0(3'b000), .in1(d_flip_flop_3_q), .out(Q), .sel(enable));
endmodule
